# Fritzing sketch sensor de temperatura (saved by Fritzing 0.9.3b)
breadboards: 1

parts:
  Componente1 = Arduino Uno (Rev3)
  LED1 = LED - 5mm [color="Red (633nm)" package="5 mm [THT]"]
  LED2 = LED - 5mm [color="Blue (430nm)" package="5 mm [THT]"]
  LED3 = LED - 5mm [color="Green (555nm)" package="5 mm [THT]"]
  T1 = TMP36 Temperature Sensor [package="TO92 [THT]"]
  R3 = Resistor [tolerance=±5% resistance=100k package=THT]
  R2 = Resistor [tolerance=±5% resistance=100k package=THT]
  R1 = Resistor [tolerance=±5% resistance=100k package=THT]

nets:
  N1: Componente1.A0, T1.Vout
  N2: Componente1.D8, R3.Pin_1
  N3: Componente1.D9_PWM, R2.Pin_1
  N4: Componente1.D10_PWM/SS, R1.Pin_1
  N5: Componente1.5V, LED1.cathode, LED2.cathode, LED3.cathode, T1.+Vs
  GND: Componente1.GND, T1.GND
  N6: LED1.anode, R3.Pin_0
  N7: LED2.anode, R1.Pin_0
  N8: LED3.anode, R2.Pin_0
